# Fritzing sketch traffic_light (saved by Fritzing 0.9.6b)
circuit board: 8.46667cm x 5.64444cm
breadboards: 1

parts:
  WeMos_D1_Mini1 = WeMos D1 Mini
  LED1 = LED - 5mm [color="Red (633nm)" current=0.030 package="5 mm [THT]"]
  LED2 = LED - 5mm [color="Orange (605nm)" current=0.030 package="5 mm [THT]"]
  LED3 = LED - 5mm [color="Green (555nm)" current=0.030 package="5 mm [THT]"]
  R1 = Resistor [tolerance=±5% resistance=220 package="2512 [SMD]"]
  R2 = Resistor [tolerance=±5% resistance=220 package="2512 [SMD]"]
  R3 = Resistor [tolerance=±5% resistance=220 package="2512 [SMD]"]
  S1 = Momentary Switch [package=ksa_sealed_tac_switch]
  J1 = Piezo Speaker  # not connected

nets:
  N1: WeMos_D1_Mini1.D5, S1.2
  N2: WeMos_D1_Mini1.D6, R1.Pin_1
  N3: WeMos_D1_Mini1.D7, R2.Pin_1
  N4: WeMos_D1_Mini1.D8, R3.Pin_1
  N5: WeMos_D1_Mini1.G, LED1.cathode, LED2.cathode, LED3.cathode, S1.3
  N6: LED1.anode, R3.Pin_0
  N7: LED2.anode, R2.Pin_0
  N8: LED3.anode, R1.Pin_0
